// Logisim project 32Sel1BuiltBy8Sel1.circ as structural Verilog: 1 circuit, main circuit main
module main (
  input  [4:0] E_D_C_B_A_input,
  output out_2
);

  wire decoder_1_out0, decoder_1_out1, decoder_1_out2, decoder_1_out3, multiplexer_1_out, multiplexer_2_out,
       multiplexer_3_out, multiplexer_4_out;

  // Probe on E_D_C_B_A_input
  // Probe on 32'hd5ba659e
  // Probe on E_D_C_B_A_input[4:3]
  // Probe on E_D_C_B_A_input[2:0]
  Decoder #(.select(2), .enable("false")) decoder_1 (
    .out0(decoder_1_out0), .out1(decoder_1_out1), .out2(decoder_1_out2), .out3(decoder_1_out3),
    .sel(E_D_C_B_A_input[4:3]));
  Multiplexer #(.select(3), .disabled(0)) multiplexer_1 (
    .in0(1'b0), .in1(1'b1), .in2(1'b1), .in3(1'b1), .in4(1'b1), .in5(1'b0), .in6(1'b0), .in7(1'b1),
    .out(multiplexer_1_out), .sel(E_D_C_B_A_input[2:0]), .en(decoder_1_out0));
  Multiplexer #(.select(3), .disabled(0)) multiplexer_2 (
    .in0(1'b1), .in1(1'b0), .in2(1'b1), .in3(1'b0), .in4(1'b0), .in5(1'b1), .in6(1'b1), .in7(1'b0),
    .out(multiplexer_2_out), .sel(E_D_C_B_A_input[2:0]), .en(decoder_1_out1));
  Multiplexer #(.select(3), .disabled(0)) multiplexer_3 (
    .in0(1'b0), .in1(1'b1), .in2(1'b0), .in3(1'b1), .in4(1'b1), .in5(1'b1), .in6(1'b0), .in7(1'b1),
    .out(multiplexer_3_out), .sel(E_D_C_B_A_input[2:0]), .en(decoder_1_out2));
  Multiplexer #(.select(3), .disabled(0)) multiplexer_4 (
    .in0(1'b1), .in1(1'b0), .in2(1'b1), .in3(1'b0), .in4(1'b1), .in5(1'b0), .in6(1'b1), .in7(1'b1),
    .out(multiplexer_4_out), .sel(E_D_C_B_A_input[2:0]), .en(decoder_1_out3));
  or or_1 (out_2, multiplexer_1_out, multiplexer_2_out, multiplexer_3_out, multiplexer_4_out);
endmodule
