// Logisim project CRC.circ as structural Verilog: 2 circuits, main circuit divider
module divider (
  input  [3:0] in_1,
  input  [3:0] in_2,
  output [2:0] out_3
);

  wire [2:0] bit_extender_1_out, xor_1_out;

  Bit_Extender #(.in_width(4), .out_width(3)) bit_extender_1 (.in(in_2), .out(bit_extender_1_out));
  Multiplexer #(.width(3), .enable("false")) multiplexer_1 (
    .in0(in_1[2:0]), .in1(xor_1_out), .out(out_3), .sel(in_1[3]));
  assign xor_1_out = in_1[2:0] ^ bit_extender_1_out;  // XOR_Gate xor_1, 3 bits wide
endmodule

module CRC (
  input  [7:0] in_1,
  input  [3:0] in_2,
  output [10:0] out_3
);

  wire [0:0] bitselector_1_out, bitselector_2_out, bitselector_3_out, bitselector_4_out;
  wire [2:0] divider_1_out_3, divider_2_out_3, divider_3_out_3, divider_4_out_3, divider_5_out_3,
       divider_6_out_3, divider_7_out_3;

  // Probe on in_1[7:4]
  BitSelector bitselector_1 (.in(in_1), .out(bitselector_1_out[0]), .sel(3'b000));
  BitSelector bitselector_2 (.in(in_1), .out(bitselector_2_out[0]), .sel(3'b001));
  BitSelector bitselector_3 (.in(in_1), .out(bitselector_3_out[0]), .sel(3'b010));
  // Probe on {divider_1_out_3, bitselector_4_out[0]}
  BitSelector bitselector_4 (.in(in_1), .out(bitselector_4_out[0]), .sel(3'b011));
  divider divider_1 (.in_1(in_1[7:4]), .in_2(in_2), .out_3(divider_1_out_3));
  // Probe on {divider_2_out_3, bitselector_3_out[0]}
  divider divider_2 (.in_1({divider_1_out_3, bitselector_4_out[0]}), .in_2(in_2), .out_3(divider_2_out_3));
  // Probe on {divider_3_out_3, bitselector_2_out[0]}
  divider divider_3 (.in_1({divider_2_out_3, bitselector_3_out[0]}), .in_2(in_2), .out_3(divider_3_out_3));
  // Probe on {divider_4_out_3, bitselector_1_out[0]}
  divider divider_4 (.in_1({divider_3_out_3, bitselector_2_out[0]}), .in_2(in_2), .out_3(divider_4_out_3));
  // Probe on {divider_5_out_3, 1'b0}
  divider divider_5 (.in_1({divider_4_out_3, bitselector_1_out[0]}), .in_2(in_2), .out_3(divider_5_out_3));
  // Probe on {divider_6_out_3, 1'b0}
  divider divider_6 (.in_1({divider_5_out_3, 1'b0}), .in_2(in_2), .out_3(divider_6_out_3));
  // Probe on {divider_7_out_3, 1'b0}
  divider divider_7 (.in_1({divider_6_out_3, 1'b0}), .in_2(in_2), .out_3(divider_7_out_3));
  divider divider_8 (.in_1({divider_7_out_3, 1'b0}), .in_2(in_2), .out_3(out_3[2:0]));

  assign out_3[10:3] = in_1;
endmodule
