// Logisim project bus.circ as structural Verilog: 2 circuits, main circuit main
module main (
  input  p1,
  input  p2,
  input  line,
  output n1,
  output n2
);

  wire and_1_out, and_2_out, and_3_out, and_4_out, not_1_out, not_2_out, not_3_out, not_4_out, not_5_out;

  not not_1 (not_1_out, p2);
  not not_2 (not_2_out, p1);
  not not_3 (not_3_out, p2);
  not not_4 (not_4_out, p2);
  not not_5 (not_5_out, p1);
  and and_1 (and_1_out, not_1_out, line);
  and and_2 (and_2_out, not_2_out, not_3_out);
  and and_3 (and_3_out, not_4_out, line);
  and and_4 (and_4_out, p1, p2);
  or or_1 (n1, not_5_out, and_1_out);
  or or_2 (n2, and_2_out, and_3_out, and_4_out);
endmodule

module bus (
  input  CLK,
  input  RESET,
  input  BUS,
  output [1:0] out_4
);

  wire [1:0] multiplexer_1_out, register_1_q;

  Multiplexer #(.width(2), .enable("false")) multiplexer_1 (
    .in0(out_4), .in1(2'b00), .out(multiplexer_1_out), .sel(RESET));
  Register #(.width(2)) register_1 (.D(multiplexer_1_out), .Q(register_1_q), .clk(CLK));  // open: en, clr
  main main_1 (.p1(register_1_q[1]), .p2(register_1_q[0]), .line(BUS), .n1(out_4[1]), .n2(out_4[0]));
endmodule
