// Logisim project fib_challenging.circ as structural Verilog: 4 circuits, main circuit main
module main (
  input  [31:0] in_1,
  output [31:0] out_2
);

  wire and_1_out, bitselector_1_out, CLK, comparator_1_eq, comparator_2_eq, comparator_3_lt;
  wire [4:0] bit_extender_1_out;
  wire [31:0] counter_1_q, matrix_1_out_9, matrix_1_out_10, matrix_1_out_11, matrix_1_out_12,
       matrix_product_1_out_9, matrix_product_1_out_10, matrix_product_1_out_11, matrix_product_1_out_12,
       matrix_product_2_out_9, matrix_product_2_out_10, matrix_product_2_out_11, matrix_product_2_out_12,
       multiplexer_1_out, multiplexer_2_out, multiplexer_3_out, multiplexer_4_out, multiplexer_5_out,
       multiplexer_6_out, multiplexer_7_out, multiplexer_8_out, multiplexer_9_out, multiplexer_10_out,
       multiplexer_11_out, multiplexer_12_out, old_pow_out_9, old_pow_out_10, old_pow_out_11, old_pow_out_12,
       subtractor_1_out, subtractor_2_out, vector_dot_product_1_out_5;

  Clock clock_1 (.out(CLK));
  Counter #(.width(32), .max('hffffffff)) counter_1 (.Q(counter_1_q), .clk(CLK));  // open: load, D, count, carry, clr
  Multiplexer #(.width(32), .enable("false")) multiplexer_1 (
    .in0(matrix_product_1_out_9), .in1(32'h1), .out(multiplexer_1_out), .sel(comparator_1_eq));
  Multiplexer #(.width(32), .enable("false")) multiplexer_2 (
    .in0(matrix_product_1_out_10), .in1(32'h1), .out(multiplexer_2_out), .sel(comparator_1_eq));
  Multiplexer #(.width(32), .enable("false")) multiplexer_3 (
    .in0(matrix_product_1_out_11), .in1(32'h1), .out(multiplexer_3_out), .sel(comparator_1_eq));
  Multiplexer #(.width(32), .enable("false")) multiplexer_4 (
    .in0(matrix_product_1_out_12), .in1({32{1'b0}}), .out(multiplexer_4_out), .sel(comparator_1_eq));
  Comparator #(.width(32)) comparator_1 (.a(32'h1), .b(counter_1_q), .eq(comparator_1_eq));  // open: gt, lt
  Subtractor #(.width(32)) subtractor_1 (.a(counter_1_q), .b(32'h2), .out(subtractor_1_out));  // open: bin, bout
  Subtractor #(.width(32)) subtractor_2 (.a(in_1), .b(32'h1), .out(subtractor_2_out));  // open: bin, bout
  // Probe on subtractor_2_out
  // Probe on subtractor_1_out
  Comparator #(.width(32), .mode("unsigned")) comparator_2 (
    .a(subtractor_1_out), .b(32'h20), .eq(comparator_2_eq));  // open: gt, lt
  // Probe on matrix_1_out_9
  matrix matrix_1 (
    .in_1(multiplexer_1_out), .in_2(multiplexer_2_out), .in_5(multiplexer_3_out), .in_6(multiplexer_4_out),
    .out_9(matrix_1_out_9), .out_10(matrix_1_out_10), .out_11(matrix_1_out_11), .out_12(matrix_1_out_12),
    .in_3(CLK), .in_4(CLK), .in_7(CLK), .in_8(CLK));
  // Probe on matrix_1_out_11
  BitSelector #(.width(32)) bitselector_1 (.in(subtractor_2_out), .out(bitselector_1_out), .sel(bit_extender_1_out));
  Bit_Extender #(.in_width(32), .out_width(5)) bit_extender_1 (.in(subtractor_1_out), .out(bit_extender_1_out));
  Comparator #(.width(32), .mode("unsigned")) comparator_3 (
    .a(subtractor_1_out), .b(32'h20), .lt(comparator_3_lt));  // open: gt, eq
  // Probe on multiplexer_5_out
  // Probe on multiplexer_7_out
  // Probe on matrix_1_out_10
  // Probe on matrix_1_out_12
  // Probe on bitselector_1_out
  // Probe on multiplexer_6_out
  // Probe on multiplexer_8_out
  and and_1 (and_1_out, bitselector_1_out, comparator_3_lt);
  Multiplexer #(.width(32), .enable("false")) multiplexer_5 (
    .in0(matrix_product_2_out_9), .in1(32'h1), .out(multiplexer_5_out), .sel(comparator_1_eq));
  Multiplexer #(.width(32), .enable("false")) multiplexer_6 (
    .in0(matrix_product_2_out_10), .in1({32{1'b0}}), .out(multiplexer_6_out), .sel(comparator_1_eq));
  Multiplexer #(.width(32), .enable("false")) multiplexer_7 (
    .in0(matrix_product_2_out_11), .in1({32{1'b0}}), .out(multiplexer_7_out), .sel(comparator_1_eq));
  Multiplexer #(.width(32), .enable("false")) multiplexer_8 (
    .in0(matrix_product_2_out_12), .in1(32'h1), .out(multiplexer_8_out), .sel(comparator_1_eq));
  Multiplexer #(.width(32), .enable("false")) multiplexer_9 (
    .in0(32'h1), .in1(matrix_1_out_9), .out(multiplexer_9_out), .sel(and_1_out));
  Multiplexer #(.width(32), .enable("false")) multiplexer_10 (
    .in0({32{1'b0}}), .in1(matrix_1_out_10), .out(multiplexer_10_out), .sel(and_1_out));
  Multiplexer #(.width(32), .enable("false")) multiplexer_11 (
    .in0({32{1'b0}}), .in1(matrix_1_out_11), .out(multiplexer_11_out), .sel(and_1_out));
  Multiplexer #(.width(32), .enable("false")) multiplexer_12 (
    .in0(32'h1), .in1(matrix_1_out_12), .out(multiplexer_12_out), .sel(and_1_out));
  matrix old_pow (
    .in_1(multiplexer_5_out), .in_2(multiplexer_6_out), .in_5(multiplexer_7_out), .in_6(multiplexer_8_out),
    .out_9(old_pow_out_9), .out_10(old_pow_out_10), .out_11(old_pow_out_11), .out_12(old_pow_out_12),
    .in_3(CLK), .in_4(CLK), .in_7(CLK), .in_8(CLK));
  matrix_product matrix_product_1 (
    .in_1(matrix_1_out_9), .in_2(matrix_1_out_10), .in_3(matrix_1_out_9), .in_4(matrix_1_out_10),
    .in_5(matrix_1_out_11), .in_6(matrix_1_out_12), .in_7(matrix_1_out_11), .in_8(matrix_1_out_12),
    .out_9(matrix_product_1_out_9), .out_10(matrix_product_1_out_10), .out_11(matrix_product_1_out_11),
    .out_12(matrix_product_1_out_12));
  // Probe on multiplexer_9_out
  // Probe on multiplexer_11_out
  matrix_product matrix_product_2 (
    .in_1(old_pow_out_9), .in_2(old_pow_out_10), .in_3(multiplexer_9_out), .in_4(multiplexer_10_out),
    .in_5(old_pow_out_11), .in_6(old_pow_out_12), .in_7(multiplexer_11_out), .in_8(multiplexer_12_out),
    .out_9(matrix_product_2_out_9), .out_10(matrix_product_2_out_10), .out_11(matrix_product_2_out_11),
    .out_12(matrix_product_2_out_12));
  // Probe on matrix_product_1_out_9
  // Probe on matrix_product_1_out_11
  // Probe on multiplexer_10_out
  // Probe on multiplexer_12_out
  // Probe on old_pow_out_9
  // Probe on old_pow_out_11
  // Probe on matrix_product_1_out_10
  // Probe on matrix_product_1_out_12
  // Probe on matrix_product_2_out_9
  // Probe on matrix_product_2_out_11
  // Probe on old_pow_out_10
  // Probe on old_pow_out_12
  // Probe on matrix_product_2_out_10
  // Probe on matrix_product_2_out_12
  vector_dot_product vector_dot_product_1 (
    .in_1(32'h1), .in_2(matrix_product_2_out_9), .in_3(matrix_product_2_out_10), .in_4({32{1'b0}}),
    .out_5(vector_dot_product_1_out_5));
  Register #(.width(32)) register_1 (
    .D(vector_dot_product_1_out_5), .en(comparator_2_eq), .Q(out_2), .clk(CLK));  // open: clr
endmodule

module vector_dot_product (
  input  [31:0] in_1,
  input  [31:0] in_2,
  input  [31:0] in_3,
  input  [31:0] in_4,
  output [31:0] out_5
);

  wire [31:0] multiplier_1_out, multiplier_2_out;

  Multiplier #(.width(32)) multiplier_1 (.a(in_2), .b(in_1), .out(multiplier_1_out));  // open: cin, cout
  Multiplier #(.width(32)) multiplier_2 (.a(in_3), .b(in_4), .out(multiplier_2_out));  // open: cin, cout
  Adder #(.width(32)) adder_1 (.a(multiplier_1_out), .b(multiplier_2_out), .out(out_5));  // open: cin, cout
endmodule

module matrix_product (
  input  [31:0] in_1,
  input  [31:0] in_2,
  input  [31:0] in_3,
  input  [31:0] in_4,
  input  [31:0] in_5,
  input  [31:0] in_6,
  input  [31:0] in_7,
  input  [31:0] in_8,
  output [31:0] out_9,
  output [31:0] out_10,
  output [31:0] out_11,
  output [31:0] out_12
);

  vector_dot_product vector_dot_product_1 (.in_1(in_3), .in_2(in_1), .in_3(in_2), .in_4(in_7), .out_5(out_9));
  vector_dot_product vector_dot_product_2 (.in_1(in_3), .in_2(in_5), .in_3(in_6), .in_4(in_7), .out_5(out_11));
  vector_dot_product vector_dot_product_3 (.in_1(in_4), .in_2(in_1), .in_3(in_2), .in_4(in_8), .out_5(out_10));
  vector_dot_product vector_dot_product_4 (.in_1(in_4), .in_2(in_5), .in_3(in_6), .in_4(in_8), .out_5(out_12));
endmodule

module matrix (
  input  [31:0] in_1,
  input  [31:0] in_2,
  input  in_3,
  input  in_4,
  input  [31:0] in_5,
  input  [31:0] in_6,
  input  in_7,
  input  in_8,
  output [31:0] out_9,
  output [31:0] out_10,
  output [31:0] out_11,
  output [31:0] out_12
);

  Register #(.width(32)) register_1 (.D(in_1), .Q(out_9), .clk(in_3));  // open: en, clr
  Register #(.width(32)) register_2 (.D(in_5), .Q(out_11), .clk(in_7));  // open: en, clr
  Register #(.width(32)) register_3 (.D(in_2), .Q(out_10), .clk(in_4));  // open: en, clr
  Register #(.width(32)) register_4 (.D(in_6), .Q(out_12), .clk(in_8));  // open: en, clr
endmodule
