// Logisim project ftoi.circ as structural Verilog: 1 circuit, main circuit ftoi
module ftoi (
  input  [15:0] in_1,
  output [31:0] out_2
);

  wire comparator_1_lt;
  wire [4:0] multiplexer_1_out, subtractor_1_out, subtractor_2_out;
  wire [31:0] bit_extender_1_out, multiplexer_2_out, negator_1_out, shifter_1_out, shifter_2_out,
       shifter_3_out;

  // Probe on in_1[14:10]
  // Probe on {1'b1, in_1[9:0]}
  assign bit_extender_1_out = {{21{1'b0}}, {1'b1, in_1[9:0]}};  // Bit_Extender bit_extender_1
  Subtractor #(.width(5)) subtractor_1 (.a(in_1[14:10]), .b(5'b01111), .out(subtractor_1_out));  // open: bin, bout
  Subtractor #(.width(5)) subtractor_2 (.a(5'b01111), .b(in_1[14:10]), .out(subtractor_2_out));  // open: bin, bout
  Comparator #(.width(5), .mode("unsigned")) comparator_1 (
    .a(in_1[14:10]), .b(5'b01111), .lt(comparator_1_lt));  // open: gt, eq
  // Probe on bit_extender_1_out
  // Probe on subtractor_1_out
  Multiplexer #(.width(5), .enable("false")) multiplexer_1 (
    .in0(subtractor_1_out), .in1(subtractor_2_out), .out(multiplexer_1_out), .sel(comparator_1_lt));
  // Probe on subtractor_2_out
  // Probe on multiplexer_1_out
  // Probe on shifter_1_out
  Shifter #(.width(32)) shifter_1 (.in(bit_extender_1_out), .\dist (multiplexer_1_out), .out(shifter_1_out));
  Shifter #(.width(32), .shift("lr")) shifter_2 (
    .in(bit_extender_1_out), .\dist (multiplexer_1_out), .out(shifter_2_out));
  // Probe on shifter_2_out
  // Probe on multiplexer_2_out
  Multiplexer #(.width(32), .enable("false")) multiplexer_2 (
    .in0(shifter_1_out), .in1(shifter_2_out), .out(multiplexer_2_out), .sel(comparator_1_lt));
  Shifter #(.width(32), .shift("ar")) shifter_3 (.in(multiplexer_2_out), .\dist (5'b01010), .out(shifter_3_out));
  Negator #(.width(32)) negator_1 (.in(shifter_3_out), .out(negator_1_out));
  Multiplexer #(.width(32), .enable("false")) multiplexer_3 (
    .in0(shifter_3_out), .in1(negator_1_out), .out(out_2), .sel(in_1[15]));
  // Probe on out_2
endmodule
