// Logisim project mod5.circ as structural Verilog: 1 circuit, main circuit mod5
module mod5 (
  input  in_1,
  output out_2,
  output out_3,
  output out_4,
  output out_5,
  output out_6
);

  wire clock_1_out;
  wire [1:1] register_1_q;

  Clock clock_1 (.out(clock_1_out));
  Register #(.width(1)) register_1 (.D(in_1), .en(1'b1), .Q(register_1_q[1]), .clk(clock_1_out));  // open: clr
  Decoder #(.select(2), .enable("false")) decoder_1 (
    .out0(out_3), .out1(out_4), .out2(out_6), .out3(out_5), .sel({register_1_q[1], in_1}));

  assign out_2 = 1'b0;
endmodule
