// Logisim project navigation.circ as structural Verilog: 3 circuits, main circuit navigation
module navigation (
  input  [1:0] DIRECTION,
  input  CLOCK,
  input  RESET,
  output ARRIVE,
  output HIT
);

  wire main_1_arrive, main_1_hit, register_2_q, RST;
  wire [1:0] main_1_next2, multiplexer_1_out, register_1_q;

  Register #(.width(2)) register_1 (.D(main_1_next2), .Q(register_1_q), .clk(CLOCK), .clr(RST));  // open: en
  // Probe on register_1_q
  Multiplexer #(.width(2), .enable("false")) multiplexer_1 (
    .in0(DIRECTION), .in1(2'b10), .out(multiplexer_1_out), .sel(RST));
  main main_1 (
    .prev1(register_1_q[1]), .prev2(register_1_q[0]), .arrive(main_1_arrive), .dir1(multiplexer_1_out[1]),
    .dir2(multiplexer_1_out[0]), .hit(main_1_hit), .next1(main_1_next2[1]), .next2(main_1_next2[0]));
  or or_1 (RST, register_2_q, RESET);
  Register #(.width(1)) register_2 (.D(main_1_arrive), .Q(register_2_q), .clk(CLOCK));  // open: en, clr
  Register #(.width(1)) register_3 (.D(main_1_hit), .Q(HIT), .clk(CLOCK), .clr(RST));  // open: en
  // Probe on main_1_next2
  Register #(.width(1)) register_4 (.D(main_1_arrive), .Q(ARRIVE), .clk(CLOCK), .clr(RESET));  // open: en

  // Other names for the same wires on the sheet: CLK = CLOCK

  // Notes on the sheet:
  //   异步复位
  //   Moore型
endmodule

module main (
  input  prev1,
  input  prev2,
  input  dir1,
  input  dir2,
  output arrive,
  output hit,
  output next1,
  output next2
);

  wire and_1_out, and_2_out, and_3_out, and_4_out, and_5_out, and_6_out, and_7_out, and_8_out, and_9_out,
       and_10_out, and_11_out, and_12_out, and_13_out, and_14_out, and_15_out, not_1_out, not_2_out,
       not_3_out, not_4_out, not_5_out, not_6_out, not_7_out, not_8_out, not_9_out, not_10_out, not_11_out,
       not_12_out, not_13_out, not_14_out, not_15_out, not_16_out, not_17_out, not_18_out, not_19_out;

  not not_1 (not_1_out, prev2);
  not not_2 (not_2_out, dir1);
  not not_3 (not_3_out, dir2);
  not not_4 (not_4_out, dir1);
  not not_5 (not_5_out, prev2);
  not not_6 (not_6_out, dir1);
  not not_7 (not_7_out, prev1);
  not not_8 (not_8_out, prev2);
  not not_9 (not_9_out, prev2);
  not not_10 (not_10_out, dir2);
  not not_11 (not_11_out, dir1);
  not not_12 (not_12_out, dir2);
  and and_1 (and_1_out, prev2, not_13_out);
  not not_13 (not_13_out, dir1);
  and and_2 (and_2_out, prev1, not_14_out, not_15_out);
  not not_14 (not_14_out, prev2);
  not not_15 (not_15_out, dir2);
  and and_3 (and_3_out, prev1, not_16_out);
  not not_16 (not_16_out, dir1);
  and and_4 (and_4_out, prev1, prev2, dir2);
  not not_17 (not_17_out, prev1);
  not not_18 (not_18_out, dir1);
  and and_5 (and_5_out, not_17_out, not_18_out, not_19_out);
  not not_19 (not_19_out, dir2);
  and and_6 (and_6_out, prev2, dir1, dir2);
  and and_7 (and_7_out, prev1, dir1, dir2);
  and and_8 (and_8_out, prev1, prev2);
  and and_9 (and_9_out, prev1, not_1_out, not_2_out, not_3_out);
  or or_1 (arrive, and_9_out, and_10_out);
  and and_10 (and_10_out, prev1, prev2, not_4_out, dir2);
  and and_11 (and_11_out, not_5_out, not_6_out, dir2);
  and and_12 (and_12_out, not_7_out, not_8_out, dir1);
  and and_13 (and_13_out, not_9_out, dir1, not_10_out);
  and and_14 (and_14_out, prev2, dir1, dir2);
  and and_15 (and_15_out, prev1, prev2, not_11_out, not_12_out);
  or or_2 (next1, and_1_out, and_2_out, and_3_out, and_4_out);
  or or_3 (next2, and_5_out, and_6_out, and_7_out, and_8_out);
  or or_4 (hit, and_11_out, and_12_out, and_13_out, and_14_out, and_15_out);
endmodule

module test (
  output arrive,
  output hit,
  output halt
);

  wire clock_1_out, counter_2_carry;
  wire [1:0] rom_1_data;
  wire [11:0] counter_1_q;

  Counter #(.width(12), .max('hfff)) counter_1 (
    .Q(counter_1_q), .carry(halt), .clk(clock_1_out));  // open: load, D, count, clr
  Clock clock_1 (.out(clock_1_out));
  ROM #(.addrWidth(12), .dataWidth(2)) rom_1 (.addr(counter_1_q), .data(rom_1_data));  // open: sel
  Counter counter_2 (.carry(counter_2_carry), .clk(clock_1_out));  // open: load, D, count, Q, clr
  // Probe on rom_1_data
  navigation navigation_1 (
    .DIRECTION(rom_1_data), .CLOCK(clock_1_out), .RESET(counter_2_carry), .ARRIVE(arrive), .HIT(hit));
  // Probe on counter_2_carry

  // Notes on the sheet:
  //   contents of rom_1 (hex, n*v repeats v):
  //   0 3 0 4*3 1 0 2 0 0 2 3 1 2 3 1 2 3 2 2 0 2 1 0 3 3 2 0 0 3
endmodule
