// Logisim project regex.circ as structural Verilog: 2 circuits, main circuit main
module main (
  input  prev1,
  input  prev2,
  input  in1,
  input  in2,
  output out,
  output next1,
  output next2
);

  wire and_2_out, and_3_out, and_4_out, and_5_out, and_6_out, and_7_out, not_1_out, not_2_out, not_3_out,
       not_4_out, not_5_out, not_6_out, not_7_out, not_8_out, not_9_out, not_10_out, not_11_out, not_12_out,
       not_13_out, not_14_out;

  and and_1 (out, prev1, prev2, not_1_out);
  not not_1 (not_1_out, in2);
  not not_2 (not_2_out, prev1);
  and and_2 (and_2_out, not_2_out, prev2, not_3_out);
  not not_3 (not_3_out, in1);
  not not_4 (not_4_out, prev1);
  and and_3 (and_3_out, not_4_out, prev2, not_5_out);
  not not_5 (not_5_out, in2);
  not not_6 (not_6_out, prev2);
  and and_4 (and_4_out, prev1, not_6_out, not_7_out);
  not not_7 (not_7_out, in2);
  not not_8 (not_8_out, prev1);
  not not_9 (not_9_out, prev2);
  not not_10 (not_10_out, in1);
  not not_11 (not_11_out, prev1);
  not not_12 (not_12_out, in2);
  not not_13 (not_13_out, prev2);
  not not_14 (not_14_out, in2);
  or or_1 (next1, and_2_out, and_3_out, and_4_out);
  and and_5 (and_5_out, not_8_out, not_9_out, not_10_out, in2);
  or or_2 (next2, and_5_out, and_6_out, and_7_out);
  and and_6 (and_6_out, not_11_out, prev2, not_12_out);
  and and_7 (and_7_out, prev1, not_13_out, not_14_out);
endmodule

module fsm (
  input  CLR,
  input  [1:0] IN,
  output OUT
);

  wire CLK;
  wire [1:0] main_1_next2, multiplexer_1_out, register_1_q;
  wire [7:0] counter_1_q;

  Counter counter_1 (.Q(counter_1_q), .clk(CLK));  // open: load, D, count, carry, clr
  ROM #(.dataWidth(2)) rom_1 (.addr(counter_1_q));  // open: data, sel
  // Probe on register_1_q
  Clock clock_1 (.out(CLK));
  main main_1 (
    .prev1(register_1_q[1]), .prev2(register_1_q[0]), .in1(IN[1]), .in2(IN[0]), .out(OUT),
    .next1(main_1_next2[1]), .next2(main_1_next2[0]));
  Multiplexer #(.width(2), .enable("false")) multiplexer_1 (
    .in0(main_1_next2), .in1(2'b00), .out(multiplexer_1_out), .sel(CLR));
  Register #(.width(2)) register_1 (.D(multiplexer_1_out), .Q(register_1_q), .clk(CLK));  // open: en, clr
  // Probe on register_1_q

  // Notes on the sheet:
  //   同步复位
  //   contents of rom_1 (hex, n*v repeats v):
  //   0 1 2 2 0 1
  //   Mealy型
endmodule
