// Logisim project swap&sort.circ as structural Verilog: 4 circuits, main circuit 1bit_swap
module _1bit_swap (
  input  I1,
  input  I2,
  input  S,
  output out_4,
  output out_5
);

  wire and_1_out, and_2_out, and_3_out, and_4_out, not_1_out, not_2_out;

  not not_1 (not_1_out, S);
  not not_2 (not_2_out, S);
  and and_1 (and_1_out, I1, not_1_out);
  and and_2 (and_2_out, I2, not_2_out);
  and and_3 (and_3_out, I2, S);
  and and_4 (and_4_out, I1, S);
  or or_1 (out_4, and_1_out, and_3_out);
  or or_2 (out_5, and_4_out, and_2_out);
endmodule

module _4bit_swap (
  input  [3:0] in_1,
  input  [3:0] in_2,
  input  in_3,
  output [3:0] out_4,
  output [3:0] out_5
);

  _1bit_swap u_1bit_swap_1 (.I1(in_1[0]), .I2(in_2[0]), .S(in_3), .out_4(out_4[0]), .out_5(out_5[0]));
  _1bit_swap u_1bit_swap_2 (.I1(in_1[1]), .I2(in_2[1]), .S(in_3), .out_4(out_4[1]), .out_5(out_5[1]));
  _1bit_swap u_1bit_swap_3 (.I1(in_1[2]), .I2(in_2[2]), .S(in_3), .out_4(out_4[2]), .out_5(out_5[2]));
  _1bit_swap u_1bit_swap_4 (.I1(in_1[3]), .I2(in_2[3]), .S(in_3), .out_4(out_4[3]), .out_5(out_5[3]));
endmodule

module _4bit_iter (
  input  [3:0] in_1,
  input  [3:0] in_2,
  input  [3:0] in_3,
  input  [3:0] in_4,
  output [3:0] out_5,
  output [3:0] out_6,
  output [3:0] out_7,
  output [3:0] out_8
);

  wire comparator_1_gt, comparator_2_gt, comparator_3_gt;
  wire [3:0] n4bit_swap_1_out_5, n4bit_swap_2_out_5;

  Comparator #(.width(4), .mode("unsigned")) comparator_1 (.a(in_1), .b(in_2), .gt(comparator_1_gt));  // open: eq, lt
  _4bit_swap u_4bit_swap_1 (
    .in_1(in_1), .in_2(in_2), .in_3(comparator_1_gt), .out_4(out_5), .out_5(n4bit_swap_1_out_5));
  // Probe on n4bit_swap_1_out_5
  Comparator #(.width(4), .mode("unsigned")) comparator_2 (
    .a(n4bit_swap_1_out_5), .b(in_3), .gt(comparator_2_gt));  // open: eq, lt
  _4bit_swap u_4bit_swap_2 (
    .in_1(n4bit_swap_1_out_5), .in_2(in_3), .in_3(comparator_2_gt), .out_4(out_6), .out_5(n4bit_swap_2_out_5));
  // Probe on n4bit_swap_2_out_5
  Comparator #(.width(4), .mode("unsigned")) comparator_3 (
    .a(n4bit_swap_2_out_5), .b(in_4), .gt(comparator_3_gt));  // open: eq, lt
  _4bit_swap u_4bit_swap_3 (
    .in_1(n4bit_swap_2_out_5), .in_2(in_4), .in_3(comparator_3_gt), .out_4(out_7), .out_5(out_8));
endmodule

module _4bit_sort (
  input  [3:0] in_1,
  input  [3:0] in_2,
  input  [3:0] in_3,
  input  [3:0] in_4,
  output [3:0] out_5,
  output [3:0] out_6,
  output [3:0] out_7,
  output [3:0] out_8
);

  wire [3:0] n4bit_iter_1_out_5, n4bit_iter_1_out_6, n4bit_iter_1_out_7, n4bit_iter_1_out_8,
       n4bit_iter_2_out_5, n4bit_iter_2_out_6, n4bit_iter_2_out_7, n4bit_iter_2_out_8;

  _4bit_iter u_4bit_iter_1 (
    .in_1(in_1), .in_2(in_2), .in_3(in_3), .in_4(in_4), .out_5(n4bit_iter_1_out_5),
    .out_6(n4bit_iter_1_out_6), .out_7(n4bit_iter_1_out_7), .out_8(n4bit_iter_1_out_8));
  _4bit_iter u_4bit_iter_2 (
    .in_1(n4bit_iter_1_out_5), .in_2(n4bit_iter_1_out_6), .in_3(n4bit_iter_1_out_7),
    .in_4(n4bit_iter_1_out_8), .out_5(n4bit_iter_2_out_5), .out_6(n4bit_iter_2_out_6),
    .out_7(n4bit_iter_2_out_7), .out_8(n4bit_iter_2_out_8));
  _4bit_iter u_4bit_iter_3 (
    .in_1(n4bit_iter_2_out_5), .in_2(n4bit_iter_2_out_6), .in_3(n4bit_iter_2_out_7),
    .in_4(n4bit_iter_2_out_8), .out_5(out_5), .out_6(out_6), .out_7(out_7), .out_8(out_8));
endmodule
