// Logisim project query_0.circ as structural Verilog: 12 circuits, main circuit test
module GRF (
  input  in_1,
  input  [4:0] in_2,
  input  [4:0] in_3,
  input  [4:0] in_4,
  input  [31:0] in_5,
  input  in_6,
  input  in_7,
  output [31:0] out_8,
  output [31:0] out_9
);

  wire [31:0] _1IN, _1OUT, _2IN, _2OUT, _3IN, _3OUT, _4IN, _4OUT, _5IN, _5OUT, _6IN, _6OUT, _7IN, _7OUT,
       _8IN, _8OUT, _9IN, _9OUT, _10IN, _10OUT, _11IN, _11OUT, _12IN, _12OUT, _13IN, _13OUT, _14IN, _14OUT,
       _15IN, _15OUT, _16IN, _16OUT, _17IN, _17OUT, _18IN, _18OUT, _19IN, _19OUT, _20IN, _20OUT, _21IN,
       _21OUT, _22IN, _22OUT, _23IN, _23OUT, _24IN, _24OUT, _25IN, _25OUT, _26IN, _26OUT, _27IN, _27OUT,
       _28IN, _28OUT, _29IN, _29OUT, _30IN, _30OUT, _31IN, _31OUT;

  Demultiplexer #(.select(5), .width(32), .tristate("true"), .enable("false")) demultiplexer_1 (
    .out1(_1IN), .out2(_2IN), .out3(_3IN), .out4(_4IN), .out5(_5IN), .out6(_6IN), .out7(_7IN), .out8(_8IN),
    .out9(_9IN), .out10(_10IN), .out11(_11IN), .out12(_12IN), .out13(_13IN), .out14(_14IN), .out15(_15IN),
    .out16(_16IN), .out17(_17IN), .out18(_18IN), .out19(_19IN), .out20(_20IN), .out21(_21IN), .out22(_22IN),
    .out23(_23IN), .out24(_24IN), .out25(_25IN), .out26(_26IN), .out27(_27IN), .out28(_28IN), .out29(_29IN),
    .out30(_30IN), .out31(_31IN), .in(in_5), .sel(in_4));  // open: out0
  Register #(.width(32)) register_1 (.D(_8IN), .en(in_1), .Q(_8OUT), .clk(in_6), .clr(in_7));
  Register #(.width(32)) register_2 (.D(_16IN), .en(in_1), .Q(_16OUT), .clk(in_6), .clr(in_7));
  Register #(.width(32)) register_3 (.D(_24IN), .en(in_1), .Q(_24OUT), .clk(in_6), .clr(in_7));
  Register #(.width(32)) register_4 (.D(_1IN), .en(in_1), .Q(_1OUT), .clk(in_6), .clr(in_7));
  Register #(.width(32)) register_5 (.D(_9IN), .en(in_1), .Q(_9OUT), .clk(in_6), .clr(in_7));
  Register #(.width(32)) register_6 (.D(_17IN), .en(in_1), .Q(_17OUT), .clk(in_6), .clr(in_7));
  Register #(.width(32)) register_7 (.D(_25IN), .en(in_1), .Q(_25OUT), .clk(in_6), .clr(in_7));
  Register #(.width(32)) register_8 (.D(_2IN), .en(in_1), .Q(_2OUT), .clk(in_6), .clr(in_7));
  Register #(.width(32)) register_9 (.D(_10IN), .en(in_1), .Q(_10OUT), .clk(in_6), .clr(in_7));
  Register #(.width(32)) register_10 (.D(_18IN), .en(in_1), .Q(_18OUT), .clk(in_6), .clr(in_7));
  Register #(.width(32)) register_11 (.D(_26IN), .en(in_1), .Q(_26OUT), .clk(in_6), .clr(in_7));
  Register #(.width(32)) register_12 (.D(_3IN), .en(in_1), .Q(_3OUT), .clk(in_6), .clr(in_7));
  Register #(.width(32)) register_13 (.D(_11IN), .en(in_1), .Q(_11OUT), .clk(in_6), .clr(in_7));
  Register #(.width(32)) register_14 (.D(_19IN), .en(in_1), .Q(_19OUT), .clk(in_6), .clr(in_7));
  Register #(.width(32)) register_15 (.D(_27IN), .en(in_1), .Q(_27OUT), .clk(in_6), .clr(in_7));
  Register #(.width(32)) register_16 (.D(_4IN), .en(in_1), .Q(_4OUT), .clk(in_6), .clr(in_7));
  Register #(.width(32)) register_17 (.D(_12IN), .en(in_1), .Q(_12OUT), .clk(in_6), .clr(in_7));
  Register #(.width(32)) register_18 (.D(_20IN), .en(in_1), .Q(_20OUT), .clk(in_6), .clr(in_7));
  Register #(.width(32)) register_19 (.D(_28IN), .en(in_1), .Q(_28OUT), .clk(in_6), .clr(in_7));
  Register #(.width(32)) register_20 (.D(_5IN), .en(in_1), .Q(_5OUT), .clk(in_6), .clr(in_7));
  Register #(.width(32)) register_21 (.D(_13IN), .en(in_1), .Q(_13OUT), .clk(in_6), .clr(in_7));
  Register #(.width(32)) register_22 (.D(_21IN), .en(in_1), .Q(_21OUT), .clk(in_6), .clr(in_7));
  Register #(.width(32)) register_23 (.D(_29IN), .en(in_1), .Q(_29OUT), .clk(in_6), .clr(in_7));
  Register #(.width(32)) register_24 (.D(_6IN), .en(in_1), .Q(_6OUT), .clk(in_6), .clr(in_7));
  Register #(.width(32)) register_25 (.D(_14IN), .en(in_1), .Q(_14OUT), .clk(in_6), .clr(in_7));
  Register #(.width(32)) register_26 (.D(_22IN), .en(in_1), .Q(_22OUT), .clk(in_6), .clr(in_7));
  Register #(.width(32)) register_27 (.D(_30IN), .en(in_1), .Q(_30OUT), .clk(in_6), .clr(in_7));
  Register #(.width(32)) register_28 (.D(_7IN), .en(in_1), .Q(_7OUT), .clk(in_6), .clr(in_7));
  Register #(.width(32)) register_29 (.D(_15IN), .en(in_1), .Q(_15OUT), .clk(in_6), .clr(in_7));
  Register #(.width(32)) register_30 (.D(_23IN), .en(in_1), .Q(_23OUT), .clk(in_6), .clr(in_7));
  Register #(.width(32)) register_31 (.D(_31IN), .en(in_1), .Q(_31OUT), .clk(in_6), .clr(in_7));
  Multiplexer #(.select(5), .width(32), .enable("false")) multiplexer_1 (
    .in0({32{1'b0}}), .in1(_1OUT), .in2(_2OUT), .in3(_3OUT), .in4(_4OUT), .in5(_5OUT), .in6(_6OUT),
    .in7(_7OUT), .in8(_8OUT), .in9(_9OUT), .in10(_10OUT), .in11(_11OUT), .in12(_12OUT), .in13(_13OUT),
    .in14(_14OUT), .in15(_15OUT), .in16(_16OUT), .in17(_17OUT), .in18(_18OUT), .in19(_19OUT), .in20(_20OUT),
    .in21(_21OUT), .in22(_22OUT), .in23(_23OUT), .in24(_24OUT), .in25(_25OUT), .in26(_26OUT), .in27(_27OUT),
    .in28(_28OUT), .in29(_29OUT), .in30(_30OUT), .in31(_31OUT), .out(out_8), .sel(in_2));
  Multiplexer #(.select(5), .width(32), .enable("false")) multiplexer_2 (
    .in0({32{1'b0}}), .in1(_1OUT), .in2(_2OUT), .in3(_3OUT), .in4(_4OUT), .in5(_5OUT), .in6(_6OUT),
    .in7(_7OUT), .in8(_8OUT), .in9(_9OUT), .in10(_10OUT), .in11(_11OUT), .in12(_12OUT), .in13(_13OUT),
    .in14(_14OUT), .in15(_15OUT), .in16(_16OUT), .in17(_17OUT), .in18(_18OUT), .in19(_19OUT), .in20(_20OUT),
    .in21(_21OUT), .in22(_22OUT), .in23(_23OUT), .in24(_24OUT), .in25(_25OUT), .in26(_26OUT), .in27(_27OUT),
    .in28(_28OUT), .in29(_29OUT), .in30(_30OUT), .in31(_31OUT), .out(out_9), .sel(in_3));

  // Other names for the same wires on the sheet: A1[4:0] = in_2; A2[4:0] = in_3; CLK = in_6; RST = in_7; WE = in_1
endmodule

module main (
  input  in_1,
  output [31:0] out_2,
  output out_3,
  output [4:0] out_4,
  output [31:0] out_5,
  output out_6,
  output [4:0] out_7,
  output [31:0] out_8
);

  wire alu_1_branch, CLK, control_1_aluamux, control_1_alubmux;
  wire [1:0] control_1_addrmux, control_1_datamux, control_1_extop, control_1_npcop, control_1_storeop;
  wire [2:0] control_1_loadop;
  wire [3:0] control_1_aluop;
  wire [4:0] im_1_out_5, im_1_out_6, im_1_out_7, im_1_out_8;
  wire [5:0] im_1_out_3, im_1_out_4;
  wire [15:0] im_1_out_9;
  wire [25:0] im_1_out_2;
  wire [31:0] bit_extender_1_out, dm_1_dataout, DMAddrTest, ext_1_out_3, grf_1_out_8, multiplexer_3_out,
       multiplexer_4_out, npc_1_npc, npc_1_pc_4, PC_q;

  Clock clock_1 (.out(CLK));
  Control control_1 (
    .NPCOp(control_1_npcop), .opcode(im_1_out_3), .funct(im_1_out_4), .rt(im_1_out_6),
    .AddrMUX(control_1_addrmux), .DataMUX(control_1_datamux), .GRFWr(out_3), .EXTOp(control_1_extop),
    .ALUAMUX(control_1_aluamux), .ALUBMUX(control_1_alubmux), .ALUOp(control_1_aluop), .Branch(alu_1_branch),
    .StoreOp(control_1_storeop), .DMWr(out_6), .LoadOp(control_1_loadop));
  Register #(.width(32)) PC (.D(npc_1_npc), .Q(PC_q), .clk(CLK), .clr(in_1));  // open: en
  NPC npc_1 (
    .Imm16(im_1_out_9), .NPCOp(control_1_npcop), .PCin(PC_q), .ra(grf_1_out_8), .NPC(npc_1_npc),
    .PC_4(npc_1_pc_4), .Imm26(im_1_out_2));
  IM im_1 (
    .in_1(PC_q), .out_3(im_1_out_3), .out_4(im_1_out_4), .out_5(im_1_out_5), .out_6(im_1_out_6),
    .out_7(im_1_out_7), .out_9(im_1_out_9), .out_2(im_1_out_2), .out_8(im_1_out_8), .out_10(out_2));
  Multiplexer #(.select(2), .width(5), .enable("false")) multiplexer_1 (
    .in0(im_1_out_6), .in1(im_1_out_7), .in2({5{1'b1}}), .out(out_4), .sel(control_1_addrmux));  // open: in3
  Multiplexer #(.select(2), .width(32), .enable("false")) multiplexer_2 (
    .in0({DMAddrTest[31:7], out_7, DMAddrTest[1:0]}), .in1(dm_1_dataout), .in2(npc_1_pc_4), .out(out_5),
    .sel(control_1_datamux));  // open: in3
  assign bit_extender_1_out = {{27{1'b0}}, im_1_out_8};  // Bit_Extender bit_extender_1
  EXT ext_1 (.in_2(im_1_out_9), .out_3(ext_1_out_3), .in_1(control_1_extop));
  GRF grf_1 (
    .in_2(im_1_out_5), .in_3(im_1_out_6), .in_4(out_4), .in_5(out_5), .out_8(grf_1_out_8), .out_9(out_8),
    .in_6(CLK), .in_7(in_1), .in_1(out_3));
  Multiplexer #(.width(32), .enable("false")) multiplexer_3 (
    .in0(grf_1_out_8), .in1(bit_extender_1_out), .out(multiplexer_3_out), .sel(control_1_aluamux));
  // Probe on multiplexer_3_out
  Multiplexer #(.width(32), .enable("false")) multiplexer_4 (
    .in0(out_8), .in1(ext_1_out_3), .out(multiplexer_4_out), .sel(control_1_alubmux));
  // Probe on multiplexer_4_out
  ALU alu_1 (
    .in_2(multiplexer_3_out), .in_3(multiplexer_4_out), .out_4({DMAddrTest[31:7], out_7, DMAddrTest[1:0]}),
    .branch(alu_1_branch), .ALUOp(control_1_aluop));
  DM dm_1 (
    .Address({DMAddrTest[31:7], out_7, DMAddrTest[1:0]}), .DataIn(out_8), .DataOut(dm_1_dataout),
    .StoreOp(control_1_storeop), .DMWr(out_6), .LoadOp(control_1_loadop), .in_5(CLK), .in_6(in_1));

  // Other names for the same wires on the sheet: DMAddrTest[6:2] = out_7; DMDataTest[31:0] = out_8; DMWrTest = out_6;
  //   GRFAddrTest[4:0] = out_4; GRFDataTest[31:0] = out_5; GRFWrTest = out_3; InstrTest[31:0] = out_2; RST = in_1

  // Notes on the sheet:
  //   Addr
  //   Data
  //   ALUA
  //   ALUB
endmodule

module ALU (
  input  [3:0] ALUOp,
  input  [31:0] in_2,
  input  [31:0] in_3,
  output [31:0] out_4,
  output branch
);

  wire comparator_1_eq, comparator_1_gt, comparator_1_lt, comparator_2_lt, comparator_3_lt, comparator_4_lt,
       not_1_out, not_2_out, not_3_out;
  wire [2:0] bit_extender_9_out;
  wire [4:0] bit_extender_1_out;
  wire [31:0] adder_1_out, and_1_out, bit_extender_2_out, bit_extender_3_out, bit_extender_4_out,
       bit_extender_5_out, bit_extender_6_out, bit_extender_7_out, bit_extender_8_out, nor_1_out, or_1_out,
       shifter_1_out, shifter_2_out, shifter_3_out, subtractor_1_out, xor_1_out;

  Bit_Extender #(.in_width(32), .out_width(5)) bit_extender_1 (.in(in_2), .out(bit_extender_1_out));
  Comparator #(.width(32)) comparator_1 (
    .a(in_2), .b(in_3), .gt(comparator_1_gt), .eq(comparator_1_eq), .lt(comparator_1_lt));
  Comparator #(.width(32)) comparator_2 (.a(in_2), .b({32{1'b0}}), .lt(comparator_2_lt));  // open: gt, eq
  Comparator #(.width(32), .mode("unsigned")) comparator_3 (.a(in_2), .b(in_3), .lt(comparator_3_lt));  // open: gt, eq
  assign and_1_out = in_2 & in_3;  // AND_Gate and_1, 32 bits wide
  assign or_1_out = in_2 | in_3;  // OR_Gate or_1, 32 bits wide
  assign nor_1_out = ~(in_2 | in_3);  // NOR_Gate nor_1, 32 bits wide
  assign xor_1_out = in_2 ^ in_3;  // XOR_Gate xor_1, 32 bits wide
  Adder #(.width(32)) adder_1 (.a(in_2), .b(in_3), .out(adder_1_out));  // open: cin, cout
  Subtractor #(.width(32)) subtractor_1 (.a(in_2), .b(in_3), .out(subtractor_1_out));  // open: bin, bout
  Shifter #(.width(32)) shifter_1 (.in(in_3), .\dist (bit_extender_1_out), .out(shifter_1_out));
  Shifter #(.width(32), .shift("lr")) shifter_2 (.in(in_3), .\dist (bit_extender_1_out), .out(shifter_2_out));
  Shifter #(.width(32), .shift("ar")) shifter_3 (.in(in_3), .\dist (bit_extender_1_out), .out(shifter_3_out));
  assign bit_extender_2_out = {{31{1'b0}}, comparator_1_gt};  // Bit_Extender bit_extender_2
  not not_1 (not_1_out, comparator_1_gt);
  assign bit_extender_3_out = {{31{1'b0}}, not_1_out};  // Bit_Extender bit_extender_3
  assign bit_extender_4_out = {{31{1'b0}}, comparator_1_eq};  // Bit_Extender bit_extender_4
  not not_2 (not_2_out, comparator_1_eq);
  assign bit_extender_5_out = {{31{1'b0}}, not_2_out};  // Bit_Extender bit_extender_5
  assign bit_extender_6_out = {{31{1'b0}}, comparator_1_lt};  // Bit_Extender bit_extender_6
  assign bit_extender_7_out = {{31{1'b0}}, not_3_out};  // Bit_Extender bit_extender_7
  not not_3 (not_3_out, comparator_2_lt);
  assign bit_extender_8_out = {{31{1'b0}}, comparator_3_lt};  // Bit_Extender bit_extender_8
  Multiplexer #(.select(4), .width(32), .enable("false")) multiplexer_1 (
    .in0(bit_extender_2_out), .in1(bit_extender_3_out), .in2(bit_extender_4_out), .in3(bit_extender_5_out),
    .in4(bit_extender_6_out), .in5(bit_extender_7_out), .in6(bit_extender_8_out), .in7(and_1_out),
    .in8(or_1_out), .in9(nor_1_out), .in10(xor_1_out), .in11(adder_1_out), .in12(subtractor_1_out),
    .in13(shifter_1_out), .in14(shifter_2_out), .in15(shifter_3_out), .out(out_4), .sel(ALUOp));
  Comparator #(.width(4), .mode("unsigned")) comparator_4 (
    .a(ALUOp), .b(4'b0101), .lt(comparator_4_lt));  // open: gt, eq
  Bit_Extender #(.in_width(4), .out_width(3)) bit_extender_9 (.in(ALUOp), .out(bit_extender_9_out));
  Multiplexer #(.select(3), .disabled(0)) multiplexer_2 (
    .in0(comparator_1_gt), .in1(not_1_out), .in2(comparator_1_eq), .in3(not_2_out), .in4(comparator_1_lt),
    .in5(not_3_out), .out(branch), .sel(bit_extender_9_out), .en(comparator_4_lt));  // open: in6, in7

  // Other names for the same wires on the sheet: in1[31:0] = in_2; in2[31:0] = in_3

  // Notes on the sheet:
  //   bgez
  //   sltu
  //   逻辑左
  //   逻辑右
  //   算术右
endmodule

module NPC (
  input  [1:0] NPCOp,
  input  [31:0] PCin,
  input  [15:0] Imm16,
  input  [31:0] ra,
  input  [25:0] Imm26,
  output [31:0] NPC,
  output [31:0] PC_4
);

  wire [31:0] adder_2_out, bit_extender_1_out, multiplier_1_out;

  assign bit_extender_1_out = {{16{Imm16[15]}}, Imm16};  // Bit_Extender bit_extender_1
  Adder #(.width(32)) adder_1 (.a(PCin), .b(32'h4), .out(PC_4));  // open: cin, cout
  Multiplier #(.width(32)) multiplier_1 (.a(32'h4), .b(bit_extender_1_out), .out(multiplier_1_out));  // open: cin, cout
  Adder #(.width(32)) adder_2 (.a(PC_4), .b(multiplier_1_out), .out(adder_2_out));  // open: cin, cout
  Multiplexer #(.select(2), .width(32), .enable("false")) multiplexer_1 (
    .in0(PC_4), .in1(adder_2_out), .in2(ra), .in3({PCin[31:28], Imm26, 2'b00}), .out(NPC), .sel(NPCOp));
endmodule

module Control (
  input  [5:0] opcode,
  input  [5:0] funct,
  input  [4:0] rt,
  input  Branch,
  output [1:0] NPCOp,
  output [1:0] AddrMUX,
  output [1:0] DataMUX,
  output GRFWr,
  output [1:0] EXTOp,
  output ALUAMUX,
  output ALUBMUX,
  output [3:0] ALUOp,
  output [1:0] StoreOp,
  output DMWr,
  output [2:0] LoadOp
);

  wire add_op, addiu, addu, \and , and_op, andi, B_2_out, B_out, beq, bgez, bgtz, blez, bltz, bne, GRFWr_out,
       j, J_out, jal, jalr, jr, lb, lbu, lh, lhu, lt_op, ltu_op, lui, lw, nop, \nor , not_1_out, \or , or_op,
       ori, R_out, sb, sh, sll, sll_op, sllv, slt, slti, sltiu, sltu, sra, sra_op, srav, srl, srl_op, srlv,
       subu, sw, \xor , xor_op, xori;

  Comparator #(.width(6), .mode("unsigned")) comparator_1 (.a(opcode), .b(6'b000100), .eq(beq));  // open: gt, lt
  Comparator #(.width(6), .mode("unsigned")) comparator_2 (.a(opcode), .b(6'b100011), .eq(lw));  // open: gt, lt
  Comparator #(.width(6), .mode("unsigned")) comparator_3 (.a(opcode), .b(6'b001111), .eq(lui));  // open: gt, lt
  InstructionR instructionr_1 (.in_1(opcode), .in_2({6{1'b0}}), .in_3(funct), .in_4(6'b100001), .out_5(addu));
  InstructionR instructionr_2 (.in_1(opcode), .in_2({6{1'b0}}), .in_3(funct), .in_4({6{1'b0}}), .out_5(sll));
  or B (B_out, beq, bgez, bgtz, blez, bltz, bne);
  or or_1 (lt_op, bltz, slti, slt);
  or or_2 (ltu_op, sltiu, sltu);
  or or_3 (and_op, andi, \and );
  or or_4 (or_op, ori, \or );
  or or_5 (xor_op, xori, \xor );
  bgez bgez_1 (.in_1(opcode), .in_2(6'b000001), .in_3(rt), .out_4(bgez));
  Comparator #(.width(6), .mode("unsigned")) comparator_4 (.a(opcode), .b(6'b101011), .eq(sw));  // open: gt, lt
  Comparator #(.width(6), .mode("unsigned")) comparator_5 (.a(opcode), .b(6'b001001), .eq(addiu));  // open: gt, lt
  InstructionR instructionr_3 (.in_1(opcode), .in_2({6{1'b0}}), .in_3(funct), .in_4(6'b100011), .out_5(subu));
  InstructionR instructionr_4 (.in_1(opcode), .in_2({6{1'b0}}), .in_3(funct), .in_4(6'b000100), .out_5(sllv));
  and B_2 (B_2_out, B_out, Branch);
  or or_6 (NPCOp[0], B_2_out, J_out);
  or u_J (J_out, j, jal);
  or or_7 (NPCOp[1], J_out, R_out);
  or R (R_out, jr, jalr);
  or or_8 (sll_op, sll, sllv);
  or or_9 (srl_op, srl, srlv);
  or or_10 (sra_op, sra, srav);
  or or_11 (add_op, addiu, addu, lui, lw, lh, lhu, lb, lbu, DMWr);
  Comparator #(.width(6), .mode("unsigned")) comparator_6 (.a(opcode), .b(6'b000111), .eq(bgtz));  // open: gt, lt
  Comparator #(.width(6), .mode("unsigned")) comparator_7 (.a(opcode), .b(6'b101001), .eq(sh));  // open: gt, lt
  Comparator #(.width(6), .mode("unsigned")) comparator_8 (.a(opcode), .b(6'b001100), .eq(andi));  // open: gt, lt
  InstructionR instructionr_5 (.in_1(opcode), .in_2({6{1'b0}}), .in_3(funct), .in_4(6'b100100), .out_5(\and ));
  InstructionR instructionr_6 (.in_1(opcode), .in_2({6{1'b0}}), .in_3(funct), .in_4(6'b000011), .out_5(sra));
  buf J_2 (AddrMUX[1], jal);  // OR_Gate
  or R_2 (AddrMUX[0], slt, sltu, \and , \or , \nor , \xor , addu, subu, sll_op, srl_op, sra_op, jalr);
  or J_R (DataMUX[1], jal, jalr);
  or I (DataMUX[0], lw, lh, lhu, lb, lbu);
  or Store (DMWr, sw, sh, sb);
  Comparator #(.width(6), .mode("unsigned")) comparator_9 (.a(opcode), .b(6'b000110), .eq(blez));  // open: gt, lt
  Comparator #(.width(6), .mode("unsigned")) comparator_10 (.a(opcode), .b(6'b101000), .eq(sb));  // open: gt, lt
  Comparator #(.width(6), .mode("unsigned")) comparator_11 (.a(opcode), .b(6'b001101), .eq(ori));  // open: gt, lt
  InstructionR instructionr_7 (.in_1(opcode), .in_2({6{1'b0}}), .in_3(funct), .in_4(6'b100111), .out_5(\nor ));
  InstructionR instructionr_8 (.in_1(opcode), .in_2({6{1'b0}}), .in_3(funct), .in_4(6'b000111), .out_5(srav));
  bltz bltz_1 (.in_1(opcode), .in_2(6'b000001), .in_3(rt), .out_4(bltz));
  Comparator #(.width(6), .mode("unsigned")) comparator_12 (.a(opcode), .b(6'b100001), .eq(lh));  // open: gt, lt
  Comparator #(.width(6), .mode("unsigned")) comparator_13 (.a(opcode), .b(6'b001110), .eq(xori));  // open: gt, lt
  InstructionR instructionr_9 (.in_1(opcode), .in_2({6{1'b0}}), .in_3(funct), .in_4(6'b100101), .out_5(\or ));
  InstructionR instructionr_10 (.in_1(opcode), .in_2({6{1'b0}}), .in_3(funct), .in_4(6'b000010), .out_5(srl));
  Comparator #(.width(6), .mode("unsigned")) comparator_14 (.a(opcode), .b(6'b000101), .eq(bne));  // open: gt, lt
  Comparator #(.width(6), .mode("unsigned")) comparator_15 (.a(opcode), .b(6'b100101), .eq(lhu));  // open: gt, lt
  Comparator #(.width(6), .mode("unsigned")) comparator_16 (.a(opcode), .b(6'b001010), .eq(slti));  // open: gt, lt
  InstructionR instructionr_11 (.in_1(opcode), .in_2({6{1'b0}}), .in_3(funct), .in_4(6'b100110), .out_5(\xor ));
  InstructionR instructionr_12 (.in_1(opcode), .in_2({6{1'b0}}), .in_3(funct), .in_4(6'b000110), .out_5(srlv));
  or Shift (ALUAMUX, sll, srl, sra);
  or I_2 (ALUBMUX, slti, sltiu, andi, ori, xori, addiu, lh, lw, lb, lhu, lbu, DMWr, lui);
  buf High (EXTOp[1], lui);  // OR_Gate
  or Signed (EXTOp[0], slti, sltiu, addiu, lw, lh, lhu, lb, lbu, DMWr);
  Comparator #(.width(6), .mode("unsigned")) comparator_17 (.a(opcode), .b(6'b000010), .eq(j));  // open: gt, lt
  Comparator #(.width(6), .mode("unsigned")) comparator_18 (.a(opcode), .b(6'b100000), .eq(lb));  // open: gt, lt
  Comparator #(.width(6), .mode("unsigned")) comparator_19 (.a(opcode), .b(6'b001011), .eq(sltiu));  // open: gt, lt
  InstructionR instructionr_13 (.in_1(opcode), .in_2({6{1'b0}}), .in_3(funct), .in_4(6'b001000), .out_5(jr));
  InstructionR instructionr_14 (.in_1(opcode), .in_2({6{1'b0}}), .in_3(funct), .in_4(6'b101010), .out_5(slt));
  Priority_Encoder #(.select(4)) priority_encoder_1 (
    .in0(bgtz), .in1(blez), .in2(beq), .in3(bne), .in4(lt_op), .in5(bgez), .in6(ltu_op), .in7(and_op),
    .in8(or_op), .in9(\nor ), .in10(xor_op), .in11(add_op), .in12(subu), .in13(sll_op), .in14(srl_op),
    .in15(sra_op), .out(ALUOp));  // open: gs, en_out, en_in
  buf Byte (StoreOp[1], sb);  // OR_Gate
  buf Half (StoreOp[0], sh);  // OR_Gate
  buf or_12 (LoadOp[2], lbu);  // OR_Gate
  or or_13 (LoadOp[1], DMWr, lw, lhu);
  or or_14 (LoadOp[0], lhu, lb);
  Comparator #(.width(6), .mode("unsigned")) comparator_20 (.a(opcode), .b(6'b000011), .eq(jal));  // open: gt, lt
  Comparator #(.width(6), .mode("unsigned")) comparator_21 (.a(opcode), .b(6'b100100), .eq(lbu));  // open: gt, lt
  InstructionR instructionr_15 (.in_1(opcode), .in_2({6{1'b0}}), .in_3(funct), .in_4(6'b001001), .out_5(jalr));
  InstructionR instructionr_16 (.in_1(opcode), .in_2({6{1'b0}}), .in_3(funct), .in_4(6'b101011), .out_5(sltu));
  InstructionR instructionr_17 (.in_1(opcode), .in_2({6{1'b0}}), .in_3(funct), .in_4({6{1'b0}}), .out_5(nop));
  or u_GRFWr (GRFWr_out, slti, slt, ltu_op, and_op, or_op, \nor , xor_op, addiu, addu, lui, lw, lh, lhu, lb, lbu, subu, sll_op, srl_op, sra_op, jal, jalr);
  and and_1 (GRFWr, GRFWr_out, not_1_out);
  not not_1 (not_1_out, DMWr);

  // Other names for the same wires on the sheet: Store = DMWr
endmodule

module EXT (
  input  [1:0] in_1,
  input  [15:0] in_2,
  output [31:0] out_3
);

  wire [31:0] bit_extender_1_out, bit_extender_2_out;

  assign bit_extender_1_out = {{16{1'b0}}, in_2};  // Bit_Extender bit_extender_1
  assign bit_extender_2_out = {{16{in_2[15]}}, in_2};  // Bit_Extender bit_extender_2
  Multiplexer #(.select(2), .width(32), .enable("false")) multiplexer_1 (
    .in0(bit_extender_1_out), .in1(bit_extender_2_out), .in2({in_2, {16{1'b0}}}), .out(out_3), .sel(in_1));  // open: in3
endmodule

module IM (
  input  [31:0] in_1,
  output [25:0] out_2,
  output [5:0] out_3,
  output [5:0] out_4,
  output [4:0] out_5,
  output [4:0] out_6,
  output [4:0] out_7,
  output [4:0] out_8,
  output [15:0] out_9,
  output [31:0] out_10
);

  ROM #(.addrWidth(5), .dataWidth(32)) rom_1 (
    .addr(in_1[6:2]), .data({out_3, out_5, out_6, out_7, out_8, out_4}));  // open: sel
  Bit_Extender #(.in_width(32), .out_width(26)) bit_extender_1 (
    .in({out_3, out_5, out_6, out_7, out_8, out_4}), .out(out_2));
  Bit_Extender #(.in_width(32)) bit_extender_2 (.in({out_3, out_5, out_6, out_7, out_8, out_4}), .out(out_9));

  assign out_10 = {out_3, out_5, out_6, out_7, out_8, out_4};

  // Notes on the sheet:
  //   contents of rom_1 (hex, n*v repeats v):
  //   36b52a88 36d61198 358c0698 36d62b08 36731dc8 ac520008 8c520008 af110014 8f110014 ac040004 8c040004
  //   acee0010 8cee0010 accc0000 8ccc0000 00940021 01943021 00c8b821 02369821 00470821 01732023 01f35023
  //   00b91823 0021c023 01e83023 3c1a60fe 3c0e71f7 3c1b5657 3c17cecf 3c124800 00000000 00000000
endmodule

module DM (
  input  [1:0] StoreOp,
  input  DMWr,
  input  [2:0] LoadOp,
  input  [31:0] Address,
  input  in_5,
  input  in_6,
  input  [31:0] DataIn,
  output [31:0] DataOut
);

  wire [7:0] bit_extender_2_out;
  wire [15:0] bit_extender_1_out, ram_1_data, ram_1_data_2;
  wire [31:0] bit_extender_3_out, bit_extender_4_out, bit_extender_5_out, bit_extender_6_out,
       bit_extender_7_out, bit_extender_8_out, bit_extender_9_out, bit_extender_10_out, bit_extender_11_out,
       bit_extender_12_out, bit_extender_13_out, bit_extender_14_out, multiplexer_1_out, multiplexer_2_out,
       multiplexer_3_out, multiplexer_4_out, multiplexer_5_out, multiplexer_6_out, multiplexer_7_out;

  Bit_Extender #(.in_width(32)) bit_extender_1 (.in(DataIn), .out(bit_extender_1_out));
  Bit_Extender #(.in_width(32), .out_width(8)) bit_extender_2 (.in(DataIn), .out(bit_extender_2_out));
  Multiplexer #(.width(32), .enable("false")) multiplexer_1 (
    .in0({ram_1_data, bit_extender_1_out}), .in1({bit_extender_1_out, ram_1_data_2}),
    .out(multiplexer_1_out), .sel(Address[1]));
  Multiplexer #(.select(2), .width(32), .enable("false")) multiplexer_2 (
    .in0({ram_1_data, ram_1_data_2[15:8], bit_extender_2_out}),
    .in1({ram_1_data, bit_extender_2_out, ram_1_data_2[7:0]}),
    .in2({ram_1_data[15:8], bit_extender_2_out, ram_1_data_2}),
    .in3({bit_extender_2_out, ram_1_data[7:0], ram_1_data_2}), .out(multiplexer_2_out), .sel(Address[1:0]));
  Multiplexer #(.select(2), .width(32), .enable("false")) multiplexer_3 (
    .in0(DataIn), .in1(multiplexer_1_out), .in2(multiplexer_2_out), .out(multiplexer_3_out), .sel(StoreOp));  // open: in3
  RAM #(.addrWidth(24), .dataWidth(32), .bus("separate")) ram_1 (
    .addr(Address[25:2]), .din(multiplexer_3_out), .data({ram_1_data, ram_1_data_2}), .str(DMWr), .clk(in_5),
    .clr(in_6));  // open: sel, ld
  assign bit_extender_3_out = {{16{1'b0}}, ram_1_data_2};  // Bit_Extender bit_extender_3
  Multiplexer #(.width(32), .enable("false")) multiplexer_4 (
    .in0(bit_extender_3_out), .in1(bit_extender_4_out), .out(multiplexer_4_out), .sel(Address[1]));
  assign bit_extender_4_out = {{16{1'b0}}, ram_1_data};  // Bit_Extender bit_extender_4
  assign bit_extender_5_out = {{24{1'b0}}, ram_1_data_2[7:0]};  // Bit_Extender bit_extender_5
  assign bit_extender_6_out = {{24{1'b0}}, ram_1_data_2[15:8]};  // Bit_Extender bit_extender_6
  Multiplexer #(.select(2), .width(32), .enable("false")) multiplexer_5 (
    .in0(bit_extender_5_out), .in1(bit_extender_6_out), .in2(bit_extender_7_out), .in3(bit_extender_8_out),
    .out(multiplexer_5_out), .sel(Address[1:0]));
  assign bit_extender_7_out = {{24{1'b0}}, ram_1_data[7:0]};  // Bit_Extender bit_extender_7
  assign bit_extender_8_out = {{24{1'b0}}, ram_1_data[15:8]};  // Bit_Extender bit_extender_8
  assign bit_extender_9_out = {{16{ram_1_data_2[15]}}, ram_1_data_2};  // Bit_Extender bit_extender_9
  Multiplexer #(.width(32), .enable("false")) multiplexer_6 (
    .in0(bit_extender_9_out), .in1(bit_extender_10_out), .out(multiplexer_6_out), .sel(Address[1]));
  assign bit_extender_10_out = {{16{ram_1_data[15]}}, ram_1_data};  // Bit_Extender bit_extender_10
  assign bit_extender_11_out = {{24{ram_1_data_2[7]}}, ram_1_data_2[7:0]};  // Bit_Extender bit_extender_11
  assign bit_extender_12_out = {{24{ram_1_data_2[15]}}, ram_1_data_2[15:8]};  // Bit_Extender bit_extender_12
  Multiplexer #(.select(2), .width(32), .enable("false")) multiplexer_7 (
    .in0(bit_extender_11_out), .in1(bit_extender_12_out), .in2(bit_extender_13_out),
    .in3(bit_extender_14_out), .out(multiplexer_7_out), .sel(Address[1:0]));
  assign bit_extender_13_out = {{24{ram_1_data[7]}}, ram_1_data[7:0]};  // Bit_Extender bit_extender_13
  assign bit_extender_14_out = {{24{ram_1_data[15]}}, ram_1_data[15:8]};  // Bit_Extender bit_extender_14
  Multiplexer #(.select(3), .width(32), .enable("false")) multiplexer_8 (
    .in0(multiplexer_4_out), .in1(multiplexer_5_out), .in2({ram_1_data, ram_1_data_2}),
    .in3(multiplexer_6_out), .in4(multiplexer_7_out), .out(DataOut), .sel(LoadOp));  // open: in5, in6, in7
endmodule

module InstructionR (
  input  [5:0] in_1,
  input  [5:0] in_2,
  input  [5:0] in_3,
  input  [5:0] in_4,
  output out_5
);

  wire comparator_1_eq, comparator_2_eq;

  Comparator #(.width(6), .mode("unsigned")) comparator_1 (.a(in_1), .b(in_2), .eq(comparator_1_eq));  // open: gt, lt
  Comparator #(.width(6), .mode("unsigned")) comparator_2 (.a(in_3), .b(in_4), .eq(comparator_2_eq));  // open: gt, lt
  and and_1 (out_5, comparator_1_eq, comparator_2_eq);
endmodule

module bgez (
  input  [5:0] in_1,
  input  [5:0] in_2,
  input  [4:0] in_3,
  output out_4
);

  wire bit_extender_1_out, comparator_1_eq;

  Comparator #(.width(6), .mode("unsigned")) comparator_1 (.a(in_1), .b(in_2), .eq(comparator_1_eq));  // open: gt, lt
  Bit_Extender #(.in_width(5), .out_width(1)) bit_extender_1 (.in(in_3), .out(bit_extender_1_out));
  and and_1 (out_4, comparator_1_eq, bit_extender_1_out);
endmodule

module bltz (
  input  [5:0] in_1,
  input  [5:0] in_2,
  input  [4:0] in_3,
  output out_4
);

  wire bit_extender_1_out, comparator_1_eq, not_1_out;

  Comparator #(.width(6), .mode("unsigned")) comparator_1 (.a(in_1), .b(in_2), .eq(comparator_1_eq));  // open: gt, lt
  not not_1 (not_1_out, bit_extender_1_out);
  Bit_Extender #(.in_width(5), .out_width(1)) bit_extender_1 (.in(in_3), .out(bit_extender_1_out));
  and and_1 (out_4, comparator_1_eq, not_1_out);
endmodule

module test (
  output [31:0] out_1,
  output out_2,
  output [4:0] out_3,
  output [31:0] out_4,
  output halt,
  output out_6,
  output [4:0] out_7,
  output [31:0] out_8
);

  wire clock_1_out, comparator_1_gt;
  wire [7:0] counter_1_q;

  Counter counter_1 (.Q(counter_1_q), .carry(halt), .clk(clock_1_out));  // open: load, D, count, clr
  Clock clock_1 (.out(clock_1_out));
  main main_1 (
    .in_1(comparator_1_gt), .out_2(out_1), .out_3(out_2), .out_4(out_3), .out_5(out_4), .out_6(out_6),
    .out_7(out_7), .out_8(out_8));
  Comparator comparator_1 (.a(8'h4), .b(counter_1_q), .gt(comparator_1_gt));  // open: eq, lt
endmodule
